# Fritzing sketch LEDs (saved by Fritzing 0.9.2b)
perfboards: 1

parts:
  U1 = 74HC595 [package="DIP16 [THT]"]
  LED1 = LED - 5mm [color="Red (633nm)" package="5 mm [THT]"]
  LED2 = LED - 5mm [color="Red (633nm)" package="5 mm [THT]"]
  LED3 = LED - 5mm [color="Red (633nm)" package="5 mm [THT]"]
  LED4 = LED - 5mm [color="Red (633nm)" package="5 mm [THT]"]
  LED5 = LED - 5mm [color="Red (633nm)" package="5 mm [THT]"]
  LED6 = LED - 5mm [color="Red (633nm)" package="5 mm [THT]"]
  LED7 = LED - 5mm [color="Red (633nm)" package="5 mm [THT]"]
  LED8 = LED - 5mm [color="Red (633nm)" package="5 mm [THT]"]
  LED9 = LED - 5mm [color="Blue (525nm)" package="5 mm [THT]"]
  R1 = Resistor [tolerance=±5% resistance=220 package=THT]
  R2 = Resistor [tolerance=±5% resistance=220 package=THT]
  R3 = Resistor [tolerance=±5% resistance=220 package=THT]
  R4 = Resistor [tolerance=±5% resistance=220 package=THT]
  R5 = Resistor [tolerance=±5% resistance=220 package=THT]
  R6 = Resistor [tolerance=±5% resistance=220 package=THT]
  R7 = Resistor [tolerance=±5% resistance=220 package=THT]
  R8 = Resistor [tolerance=±5% resistance=220 package=THT]
  R9 = Resistor [tolerance=±5% resistance=220 package=THT]
  U2 = attiny85 [package=dip]
  U3 = attiny85 [package=dip]
  Part1 = Arduino Uno (Rev3)
  C1 = Electrolytic Capacitor [capacitance=10µF package="100 mil [THT, electrolytic]"]

nets:
  N1: U1.Q1, LED2.anode
  N2: U1.Q2, LED4.anode
  N3: U1.Q3, LED3.anode
  N4: U1.Q4, LED6.anode
  N5: U1.Q5, LED8.anode
  N6: U1.Q6, LED7.anode
  N7: U1.Q7, LED5.anode
  GND: U1.GND, R1.Pin_1, R2.Pin_1, R3.Pin_1, R4.Pin_1, R5.Pin_1, R6.Pin_1, R7.Pin_1, R8.Pin_1, R9.Pin_1, U2.Pin_4
  N8: U1.Q7', LED9.anode
  N9: U1.SH_CP, U2.Pin_7
  N10: U1.ST_CP, U2.Pin_6
  N11: U1.DS, U2.Pin_5
  N12: U1.Q0, LED1.anode
  5V: U1.VCC, U2.Pin_8
  N13: LED1.cathode, R1.Pin_0
  N14: LED2.cathode, R2.Pin_0
  N15: LED3.cathode, R3.Pin_0
  N16: LED4.cathode, R4.Pin_0
  N17: LED5.cathode, R6.Pin_0
  N18: LED6.cathode, R5.Pin_0
  N19: LED7.cathode, R8.Pin_0
  N20: LED8.cathode, R7.Pin_0
  N21: LED9.cathode, R9.Pin_0
  N22: U3.Pin_1, Part1.D10_PWM/SS
  N23: U3.Pin_4, Part1.GND, C1.-
  N24: U3.Pin_5, Part1.D11_PWM/MOSI
  N25: U3.Pin_6, Part1.D12/MISO
  N26: U3.Pin_7, Part1.D13/SCK
  N27: U3.Pin_8, Part1.5V
  N28: Part1.RESET, C1.+
